# Fritzing sketch Si4703_Itsy_M0 (saved by Fritzing 0.9.3b)
breadboards: 1

parts:
  U1 = SI470X [package=si470x]  # not connected
  S1 = Pushbutton [package="[THT]"]  # not connected
  S2 = Pushbutton [package="[THT]"]  # not connected
  S3 = Pushbutton [package="[THT]"]
  S4 = Pushbutton [package="[THT]"]
  R1 = Rotary Potentiometer (Small) [maximum_resistance=100kΩ package=THT]
  U3 = LCD-16X2 [package=lcd-16x2]
  Part2 = Digital FM Radio Receiver
  R2 = Resistor [tolerance=±5% resistance=10k package=THT]
  R3 = Resistor [tolerance=±5% resistance=10k package=THT]
  Part3 = Itsy Bitsy M0 Express

nets:
  VDD: S3.Pin_1, S3.Pin_2, S4.Pin_1, S4.Pin_2, U3.VDD, U3.A, Part2.3.3V, Part3.+3V3
  N1: S3.Pin_3, S3.Pin_4, R3.Pin_1, Part3.D3
  N2: S4.Pin_3, S4.Pin_4, R2.Pin_1, Part3.D4
  GND: R1.wiper, U3.VSS, U3.VO, U3.R_W, U3.K, Part2.GND, R2.Pin_0, R3.Pin_0, Part3.GND
  N3: U3.RS, Part3.D7
  N4: U3.E, Part3.D9
  N5: U3.DB4, Part3.D10
  N6: U3.DB5, Part3.D11
  N7: U3.DB6, Part3.D12
  N8: U3.DB7, Part3.D13
  N9: Part2.!RST, Part3.D2
  N10: Part2.SCLK, Part3.SCL
  N11: Part2.SDIO, Part3.SDA

custom parts:
  Itsy Bitsy M0 Express: What's smaller than a Feather but larger than a Trinket? It's an Adafruit ItsyBitsy M0 Express! Small, powerful, with a rockin' ATSAMD21 Cortex M0 processor running at 48 MHz - this microcontroller board is perfect when you want something very compact, but still with a bunch of pins. ItsyBitsy M0 Express is only 1.4" long by 0.7" wide, but has 6 power pins, 23 digital GPIO pins (12 of which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
